# Fritzing sketch Alarm (saved by Fritzing 0.7.10b)
breadboards: 1

parts:
  Netduino1 = Netduino Plus
  LED2 = LED - 3mm [color="Red (633nm)" package="3 mm [THT]"]
  LED1 = LED - 3mm [color="Red (633nm)" package="3 mm [THT]"]
  LED3 = LED - 3mm [color="Red (633nm)" package="3 mm [THT]"]
  R1 = 470 Ω Resistor [package=THT]
  R2 = 470 Ω Resistor [package=THT]
  R3 = 470 Ω Resistor [package=THT]
  R4 = 470 Ω Resistor [package=THT]
  R5 = 470 Ω Resistor [package=THT]
  R6 = 470 Ω Resistor [package=THT]
  R7 = 470 Ω Resistor [package=THT]
  R8 = 470 Ω Resistor [package=THT]
  R9 = 470 Ω Resistor [package=THT]
  LED4 = LED - 3mm [color="Red (633nm)" package="3 mm [THT]"]
  LED5 = LED - 3mm [color="Red (633nm)" package="3 mm [THT]"]
  LED6 = LED - 3mm [color="Red (633nm)" package="3 mm [THT]"]
  LED7 = LED - 3mm [color="Red (633nm)" package="3 mm [THT]"]
  LED8 = LED - 3mm [color="Red (633nm)" package="3 mm [THT]"]
  LED9 = LED - 3mm [color="Red (633nm)" package="3 mm [THT]"]

nets:
  N1: Netduino1.GND, LED2.cathode, LED1.cathode, LED3.cathode, LED4.cathode, LED5.cathode, LED6.cathode, LED7.cathode, LED8.cathode, LED9.cathode
  N2: Netduino1.D8_CTS1, R9.Pin_1
  N3: Netduino1.D7_RTS1, R8.Pin_1
  N4: Netduino1.D6_PWM1, R7.Pin_1
  N5: Netduino1.D5_PWM0, R6.Pin_1
  N6: Netduino1.D4_CS0, R5.Pin_1
  N7: Netduino1.D3_TX1, R4.Pin_1
  N8: Netduino1.D2_RX1, R3.Pin_1
  N9: Netduino1.D1_TX0, R2.Pin_1
  N10: Netduino1.D0_RX0, R1.Pin_1
  N11: LED2.anode, R2.Pin_0
  N12: LED1.anode, R1.Pin_0
  N13: LED3.anode, R3.Pin_0
  N14: R4.Pin_0, LED4.anode
  N15: R5.Pin_0, LED5.anode
  N16: R6.Pin_0, LED6.anode
  N17: R7.Pin_0, LED7.anode
  N18: R8.Pin_0, LED8.anode
  N19: R9.Pin_0, LED9.anode

notes:
  LED1 - Alarm
  LED2 - Master Bedroom Window circuit
  LED3 - Bedroom 1 Window circuit
  LED4 - Bedroom 2 Window circuit
  LED5 - First Floor Window circuit
  LED6 - First Floor Motion circuit
  LED7 - Front Door circuit
  LED8 - Back Door circuit
  LED9 - Side Door circuit
