# Fritzing sketch AlarmPanel (saved by Fritzing 0.7.10b)
breadboards: 1

parts:
  Netduino1 = Netduino Plus
  LED1 = LED - 3mm [color="Red (633nm)" package="3 mm [THT]"]
  LED2 = LED - 3mm [color="Red (633nm)" package="3 mm [THT]"]
  LED3 = LED - 3mm [color="Red (633nm)" package="3 mm [THT]"]
  R1 = 470 Ω Resistor [package=THT]
  R2 = 470 Ω Resistor [package=THT]
  R3 = 470 Ω Resistor [package=THT]
  S1 = Pushbutton [package=THT]
  S3 = Pushbutton [package=THT]
  S4 = Pushbutton [package=THT]
  S5 = Pushbutton [package=THT]
  S6 = Pushbutton [package=THT]
  S7 = Pushbutton [package=THT]
  S3_2 = Pushbutton [package=THT]

nets:
  N1: Netduino1.GND, LED1.cathode, LED2.cathode, LED3.cathode, S1.leg1, S3.leg1, S4.leg1, S5.leg1, S6.leg1, S7.leg1, S3_2.leg1
  N2: Netduino1.D9_PWM2, S7.leg0
  N3: Netduino1.D8_CTS1, S6.leg0
  N4: Netduino1.D7_RTS1, S5.leg0
  N5: Netduino1.D6_PWM1, S4.leg0
  N6: Netduino1.D5_PWM0, S3.leg0
  N7: Netduino1.D4_CS0, S3_2.leg0
  N8: Netduino1.D3_TX1, S1.leg0
  N9: Netduino1.D2_RX1, R3.Pin_0
  N10: Netduino1.D1_TX0, R2.Pin_0
  N11: Netduino1.D0_RX0, R1.Pin_0
  N12: LED1.anode, R1.Pin_1
  N13: LED2.anode, R2.Pin_1
  N14: LED3.anode, R3.Pin_1

notes:
  S1 - Window circuit
  S2 - Key 0
  S3 - Key 1
  S4 - Key Enter
  S5 - Motion circuit
  S6 - Alarm Mode Sleep
  S7 - Alarm Mode Away
  LED1 - Alarm Mode Away
  LED2 - Alarm Mode Sleep
  LED3 - Invalid Code
