# Fritzing sketch Doorbell (saved by Fritzing 0.7.10b)
breadboards: 1

parts:
  Netduino1 = Netduino Plus
  LED2 = LED - 3mm [color="Red (633nm)" package="3 mm [THT]"]
  LED1 = LED - 3mm [color="Red (633nm)" package="3 mm [THT]"]
  LED3 = LED - 3mm [color="Red (633nm)" package="3 mm [THT]"]
  R1 = 470 Ω Resistor [package=THT]
  R2 = 470 Ω Resistor [package=THT]
  R3 = 470 Ω Resistor [package=THT]

nets:
  N1: Netduino1.GND, LED2.cathode, LED1.cathode, LED3.cathode
  N2: Netduino1.D2_RX1, R3.Pin_1
  N3: Netduino1.D1_TX0, R2.Pin_1
  N4: Netduino1.D0_RX0, R1.Pin_1
  N5: LED2.anode, R2.Pin_0
  N6: LED1.anode, R1.Pin_0
  N7: LED3.anode, R3.Pin_0

notes:
  LED1 - Front Doorbell
  LED2 - Back Doorbell
  LED3 - Side Doorbell
