# Fritzing sketch ExternalDoor (saved by Fritzing 0.7.10b)
breadboards: 1

parts:
  Netduino1 = Netduino Plus
  LED2 = LED - 3mm [color="Red (633nm)" package="3 mm [THT]"]
  LED1 = LED - 3mm [color="Red (633nm)" package="3 mm [THT]"]
  R1 = 470 Ω Resistor [package=THT]
  R2 = 470 Ω Resistor [package=THT]
  S3 = Pushbutton [package=THT]
  S4 = Pushbutton [package=THT]
  S5 = Pushbutton [package=THT]
  S1 = Pushbutton [package=THT]
  S2 = Pushbutton [package=THT]

nets:
  N1: Netduino1.GND, LED2.cathode, LED1.cathode, S3.leg1, S4.leg1, S5.leg1, S1.leg1, S2.leg1
  N2: Netduino1.D6_PWM1, S5.leg0
  N3: Netduino1.D5_PWM0, S4.leg0
  N4: Netduino1.D4_CS0, S3.leg0
  N5: Netduino1.D3_TX1, S2.leg0
  N6: Netduino1.D2_RX1, S1.leg0
  N7: Netduino1.D1_TX0, R2.Pin_1
  N8: Netduino1.D0_RX0, R1.Pin_1
  N9: LED2.anode, R2.Pin_0
  N10: LED1.anode, R1.Pin_0

notes:
  LED1 - Door Locked
  LED2 - Invalid Code
  S1 - Door
  S2 - Key 0
  S3 - Key 1
  S4 - Key Enter
  S5 - Doorbell
